// Logisim project ex4.circ as structural Verilog: 1 circuit, main circuit Split
module Split (
  input  [7:0] In1,
  output Out1,
  output [7:0] Out2
);

  wire [6:0] not_1_out;

  assign not_1_out = ~In1[6:0];  // NOT_Gate not_1, 7 bits wide
  and and_1 (Out1, In1[0], In1[7]);
  Adder #(.width(7)) adder_1 (.a(not_1_out), .b(7'b0000001), .out(Out2[6:0]));  // open: cin, cout

  assign Out2[7] = In1[7];

  // Notes on the sheet:
  //   PUT CIRCUITRY HERE
endmodule
