// Logisim project ex5.circ as structural Verilog: 5 circuits, main circuit rotr
module rotr (
  input  [15:0] A,
  input  [3:0] B,
  output [15:0] Out1
);

  wire [15:0] multiplexer_1_out, multiplexer_2_out, multiplexer_3_out;

  // Probe on {A[0], A[15:1]}
  // Probe on A
  // Probe on multiplexer_1_out
  Multiplexer #(.width(16), .enable("false")) multiplexer_1 (
    .in0(A), .in1({A[0], A[15:1]}), .out(multiplexer_1_out), .sel(B[0]));
  Multiplexer #(.width(16), .enable("false")) multiplexer_2 (
    .in0(multiplexer_1_out), .in1({multiplexer_1_out[1:0], multiplexer_1_out[15:2]}),
    .out(multiplexer_2_out), .sel(B[1]));
  Multiplexer #(.width(16), .enable("false")) multiplexer_3 (
    .in0(multiplexer_2_out), .in1({multiplexer_2_out[3:0], multiplexer_2_out[15:4]}),
    .out(multiplexer_3_out), .sel(B[2]));
  Multiplexer #(.width(16), .enable("false")) multiplexer_4 (
    .in0(multiplexer_3_out), .in1({multiplexer_3_out[7:0], multiplexer_3_out[15:8]}), .out(Out1), .sel(B[3]));

  // Notes on the sheet:
  //   PUT CIRCUITRY HERE
endmodule

module rot8 (
  input  [15:0] in_1,
  output [15:0] out_2
);


  assign out_2 = {in_1[7:0], in_1[15:8]};

  // Notes on the sheet:
  //   PUT CIRCUITRY HERE
endmodule

module rot4 (
  input  [15:0] in_1,
  output [15:0] out_2
);


  assign out_2 = {in_1[3:0], in_1[15:4]};

  // Notes on the sheet:
  //   PUT CIRCUITRY HERE
endmodule

module rot2 (
  input  [15:0] in_1,
  output [15:0] out_2
);


  assign out_2 = {in_1[1:0], in_1[15:2]};

  // Notes on the sheet:
  //   PUT CIRCUITRY HERE
endmodule

module rot1 (
  input  [15:0] in_1,
  output [15:0] out_2
);


  assign out_2 = {in_1[0], in_1[15:1]};

  // Notes on the sheet:
  //   PUT CIRCUITRY HERE
endmodule
