// Logisim project regfile.circ as structural Verilog: 1 circuit, main circuit main
module main (
  input  [4:0] rs1,
  input  [4:0] rs2,
  input  [4:0] rd,
  input  [31:0] Write_Data,
  input  RegWEn,
  input  clk,
  output [31:0] ra,
  output [31:0] sp,
  output [31:0] t0,
  output [31:0] t1,
  output [31:0] t2,
  output [31:0] s0,
  output [31:0] s1,
  output [31:0] a0,
  output [31:0] Read_Data_1,
  output [31:0] Read_Data_2
);

  wire and_1_out, and_2_out, and_3_out, and_4_out, and_5_out, and_6_out, and_7_out, and_8_out, w0, w1, w2,
       w3, w4, w5, w6, w7, w8, w9, w10, w11, w12, w13, w14, w15, w16, w17, w18, w19, w20, w21, w22, w23, w24,
       w25, w26, w27, w28, w29, w30, w31;
  wire [31:0] multiplexer_2_out, multiplexer_3_out, multiplexer_4_out, multiplexer_5_out, multiplexer_6_out,
       multiplexer_7_out, multiplexer_8_out, reg_0, reg_3, reg_4, reg_5, reg_6, reg_7, reg_8, reg_9, reg_10,
       reg_11, reg_12, reg_13, reg_14, reg_15, reg_16, reg_17, reg_18, reg_19, reg_20, reg_21, reg_22,
       reg_23, reg_24, reg_25, reg_26, reg_27, reg_28, reg_29, reg_30, reg_31;

  and and_1 (and_1_out, w4, RegWEn);
  Multiplexer #(.width(32), .enable("false")) multiplexer_1 (
    .in0(Write_Data), .in1(a0), .out(Write_Data), .sel(and_2_out));
  and and_2 (and_2_out, w4, RegWEn);
  Register #(.width(32)) register_1 (.D(reg_0), .clk(clk), .Q(reg_0));  // open: en, clr
  Multiplexer #(.width(32), .enable("false")) multiplexer_2 (
    .in0(Write_Data), .in1(t1), .out(multiplexer_2_out), .sel(and_1_out));
  Register #(.width(32)) register_2 (.D(multiplexer_2_out), .clk(clk), .Q(t1));  // open: en, clr
  Register #(.width(32)) register_3 (.D(Write_Data), .clk(clk), .Q(a0));  // open: en, clr
  Multiplexer #(.width(32), .enable("false")) multiplexer_3 (
    .in0(Write_Data), .in1(ra), .out(multiplexer_3_out), .sel(and_3_out));
  and and_3 (and_3_out, w1, RegWEn);
  Register #(.width(32)) register_4 (.D(multiplexer_3_out), .clk(clk), .Q(ra));  // open: en, clr
  Multiplexer #(.width(32), .enable("false")) multiplexer_4 (
    .in0(Write_Data), .in1(t2), .out(multiplexer_4_out), .sel(and_4_out));
  and and_4 (and_4_out, w5, RegWEn);
  Register #(.width(32)) register_5 (.D(multiplexer_4_out), .clk(clk), .Q(t2));  // open: en, clr
  and and_5 (and_5_out, w2, RegWEn);
  Multiplexer #(.width(32), .enable("false")) multiplexer_5 (
    .in0(Write_Data), .in1(s0), .out(multiplexer_5_out), .sel(and_6_out));
  and and_6 (and_6_out, w6, RegWEn);
  Register #(.width(32)) register_6 (.D(multiplexer_5_out), .clk(clk), .Q(s0));  // open: en, clr
  Multiplexer #(.width(32), .enable("false")) multiplexer_6 (
    .in0(Write_Data), .in1(sp), .out(multiplexer_6_out), .sel(and_5_out));
  Register #(.width(32)) register_7 (.D(multiplexer_6_out), .clk(clk), .Q(sp));  // open: en, clr
  Multiplexer #(.width(32), .enable("false")) multiplexer_7 (
    .in0(Write_Data), .in1(s1), .out(multiplexer_7_out), .sel(and_7_out));
  and and_7 (and_7_out, w7, RegWEn);
  Multiplexer #(.width(32), .enable("false")) multiplexer_8 (
    .in0(Write_Data), .in1(t0), .out(multiplexer_8_out), .sel(and_8_out));
  and and_8 (and_8_out, w3, RegWEn);
  Register #(.width(32)) register_8 (.D(multiplexer_7_out), .clk(clk), .Q(s1));  // open: en, clr
  Register #(.width(32)) register_9 (.D(multiplexer_8_out), .clk(clk), .Q(t0));  // open: en, clr
  Multiplexer #(.select(5), .width(32), .enable("false")) multiplexer_9 (
    .in0(reg_0), .in1(ra), .in2(sp), .in3(reg_3), .in4(reg_4), .in5(reg_5), .in6(reg_6), .in7(reg_7),
    .in8(reg_8), .in9(reg_9), .in10(reg_10), .in11(reg_11), .in12(reg_12), .in13(reg_13), .in14(reg_14),
    .in15(reg_15), .in16(reg_16), .in17(reg_17), .in18(reg_18), .in19(reg_19), .in20(reg_20), .in21(reg_21),
    .in22(reg_22), .in23(reg_23), .in24(reg_24), .in25(reg_25), .in26(reg_26), .in27(reg_27), .in28(reg_28),
    .in29(reg_29), .in30(reg_30), .in31(reg_31), .out(Read_Data_1), .sel(rs1));
  Multiplexer #(.select(5), .width(32), .enable("false")) multiplexer_10 (
    .in0(reg_0), .in1(ra), .in2(sp), .in3(reg_3), .in4(reg_4), .in5(reg_5), .in6(reg_6), .in7(reg_7),
    .in8(reg_8), .in9(reg_9), .in10(reg_10), .in11(reg_11), .in12(reg_12), .in13(reg_13), .in14(reg_14),
    .in15(reg_15), .in16(reg_16), .in17(reg_17), .in18(reg_18), .in19(reg_19), .in20(reg_20), .in21(reg_21),
    .in22(reg_22), .in23(reg_23), .in24(reg_24), .in25(reg_25), .in26(reg_26), .in27(reg_27), .in28(reg_28),
    .in29(reg_29), .in30(reg_30), .in31(reg_31), .out(Read_Data_2), .sel(rs2));
  Demultiplexer #(.select(5), .enable("false")) demultiplexer_1 (
    .out0(w0), .out1(w1), .out2(w2), .out3(w3), .out4(w4), .out5(w5), .out6(w6), .out7(w7), .out8(w8),
    .out9(w9), .out10(w10), .out11(w11), .out12(w12), .out13(w13), .out14(w14), .out15(w15), .out16(w16),
    .out17(w17), .out18(w18), .out19(w19), .out20(w20), .out21(w21), .out22(w22), .out23(w23), .out24(w24),
    .out25(w25), .out26(w26), .out27(w27), .out28(w28), .out29(w29), .out30(w30), .out31(w31), .in(1'b1),
    .sel(rd));
  // Probe on w31
  // also tied to GND on the sheet: {reg_0[0], reg_0[1], reg_0[2], reg_0[3], reg_0[4], reg_0[5], reg_0[6], reg_0[7], reg_0[8], reg_0[9], reg_0[10], reg_0[11], reg_0[12], reg_0[13], reg_0[14], reg_0[15], reg_0[16], reg_0[17], reg_0[18], reg_0[19], reg_0[20], reg_0[21], reg_0[22], reg_0[23], reg_0[24], reg_0[25], reg_0[26], reg_0[27], reg_0[28], reg_0[29], reg_0[30], reg_0[31]}

  // Other names for the same wires on the sheet: read_data1[31:0] = Read_Data_1; read_data2[31:0] = Read_Data_2;
  //   read_reg1[4:0] = rs1; read_reg2[4:0] = rs2; write_en = RegWEn; write_reg[4:0] = rd

  // Notes on the sheet:
  //   INPUTS to your circuit
  //   DON'T CHANGE THE LOCATIONS OF THE INPUTS AND OUTPUTS!
  //   These are DEBUG/TEST outputs from your circuit.
  //   OUTPUTS from your circuit
endmodule
