// Logisim project alu.circ as structural Verilog: 1 circuit, main circuit alu
module alu (
  input  [31:0] A,
  input  [31:0] B,
  input  [3:0] ALUSel,
  output [31:0] Result
);

  wire comparator_1_lt;
  wire [31:0] add0, adder_2_out, and1, divu8, mul_10, mulh_14, mulhu_11, multiplier_2_out, multiplier_3_cout,
       multiplier_4_out, or2, remu9, shifter_4_out, shifter_5_out, sll6, slt7, sra5, srl4, sub_12, xor3;

  Adder #(.width(32)) adder_1 (.a(A), .b(B), .out(add0));  // open: cin, cout
  assign and1 = A & B;  // AND_Gate and_1, 32 bits wide
  assign or2 = A | B;  // OR_Gate or_1, 32 bits wide
  assign xor3 = A ^ B;  // XOR_Gate xor_1, 32 bits wide
  Shifter #(.width(32), .shift("lr")) shifter_1 (.in(A), .\dist (B[4:0]), .out(srl4));
  Shifter #(.width(32), .shift("ar")) shifter_2 (.in(A), .\dist (B[4:0]), .out(sra5));
  Shifter #(.width(32)) shifter_3 (.in(A), .\dist (B[4:0]), .out(sll6));
  Comparator #(.width(32)) comparator_1 (.a(A), .b(B), .lt(comparator_1_lt));  // open: gt, eq
  assign slt7 = {{31{1'b0}}, comparator_1_lt};  // Bit_Extender bit_extender_1
  // Probe on mulhu_11
  // Probe on shifter_4_out
  Shifter #(.width(32), .shift("ar")) shifter_4 (.in(A), .\dist ({5{1'b1}}), .out(shifter_4_out));
  Shifter #(.width(32), .shift("ar")) shifter_5 (.in(B), .\dist ({5{1'b1}}), .out(shifter_5_out));
  // Probe on shifter_5_out
  Divider #(.width(32)) divider_1 (.a(A), .b(B), .out(divu8), .rem(remu9));  // open: upper
  // Probe on mul_10
  Multiplier #(.width(32)) multiplier_1 (.a(A), .b(B), .out(mul_10), .cout(mulhu_11));  // open: cin
  Subtractor #(.width(32)) subtractor_1 (.a(A), .b(B), .out(sub_12));  // open: bin, bout
  Multiplier #(.width(32)) multiplier_2 (.a(shifter_4_out), .b(B), .out(multiplier_2_out));  // open: cin, cout
  Multiplier #(.width(32)) multiplier_3 (.a(A), .b(B), .cout(multiplier_3_cout));  // open: out, cin
  Multiplier #(.width(32)) multiplier_4 (.a(A), .b(shifter_5_out), .out(multiplier_4_out));  // open: cin, cout
  // Probe on multiplier_4_out
  // Probe on multiplier_2_out
  // Probe on multiplier_3_cout
  Adder #(.width(32)) adder_2 (.a(multiplier_2_out), .b(multiplier_3_cout), .out(adder_2_out));  // open: cin, cout
  Adder #(.width(32)) adder_3 (.a(adder_2_out), .b(multiplier_4_out), .out(mulh_14));  // open: cin, cout
  // Probe on mulh_14
  Multiplexer #(.select(4), .width(32), .enable("false")) multiplexer_1 (
    .in0(add0), .in1(and1), .in2(or2), .in3(xor3), .in4(srl4), .in5(sra5), .in6(sll6), .in7(slt7),
    .in8(divu8), .in9(remu9), .in10(mul_10), .in11(mulhu_11), .in12(sub_12), .in13(B), .in14(mulh_14),
    .out(Result), .sel(ALUSel));  // open: in15

  // Other names for the same wires on the sheet: bsel_13[31:0] = B

  // Notes on the sheet:
  //   INPUTS to your circuit
  //   DON'T CHANGE THE LOCATIONS OF THE INPUTS AND OUTPUTS!
  //   OUTPUT from your circuit
endmodule
