// Logisim project cpu.circ as structural Verilog: 1 circuit, main circuit main
module main (
  input  [31:0] INSTRUCTION,
  input  CLOCK,
  output [31:0] PROGRAM_COUNTER,
  output [31:0] ra,
  output [31:0] sp,
  output [31:0] t0,
  output [31:0] t1,
  output [31:0] t2,
  output [31:0] s0,
  output [31:0] s1,
  output [31:0] a0
);

  wire control_logic_1_regwen;
  wire [3:0] control_logic_1_alusel;
  wire [31:0] adder_1_out, Arithmetic_Logic_Unit_result, imm_gen_1_imm, RegFile_read_data_1, register_1_q;

  control_logic control_logic_1 (
    .RegWEn(control_logic_1_regwen), .ALUSel(control_logic_1_alusel));  // open: BSel, ASel, ImmSel, BrUn, PCSel, BrLt, BrEq, inst, MemRW, WBSel
  Adder #(.width(32)) adder_1 (.a(PROGRAM_COUNTER), .b(32'h4), .out(adder_1_out));  // open: cin, cout
  Register #(.width(32)) PC (.D(adder_1_out), .clk(CLOCK), .Q(PROGRAM_COUNTER));  // open: en, clr
  Register #(.width(32)) register_1 (.D(INSTRUCTION), .clk(CLOCK), .Q(register_1_q));  // open: en, clr
  // Probe on register_1_q[11:7]
  // Probe on register_1_q[19:15]
  imm_gen imm_gen_1 (.inst(register_1_q), .imm(imm_gen_1_imm));  // open: ImmSel
  // Probe on control_logic_1_regwen
  regfile_main RegFile (
    .rd(register_1_q[11:7]), .Read_Data_1(RegFile_read_data_1), .ra(ra), .sp(sp), .t0(t0), .t1(t1), .t2(t2),
    .s0(s0), .s1(s1), .a0(a0), .rs1(register_1_q[19:15]), .Write_Data(Arithmetic_Logic_Unit_result),
    .RegWEn(control_logic_1_regwen), .clk(CLOCK));  // open: rs2, Read_Data_2
  // Probe on Arithmetic_Logic_Unit_result
  alu Arithmetic_Logic_Unit (
    .ALUSel(control_logic_1_alusel), .Result(Arithmetic_Logic_Unit_result), .A(RegFile_read_data_1),
    .B(imm_gen_1_imm));
  // branch_comp branch_comp_1: pin names not known
  // mem_main DMEM: pin names not known

  // Other names for the same wires on the sheet: clk = CLOCK

  // Notes on the sheet:
  //   Output
  //   IMEM (do **NOT** move this)
  //   Inputs
  //   Inputs/Outputs for testing. Do **NOT** move these.
endmodule
