// Logisim project regfile.circ as structural Verilog: 1 circuit, main circuit main
module main (
  input  [4:0] rs1,
  input  [4:0] rs2,
  input  [4:0] rd,
  input  [31:0] Write_Data,
  input  RegWEn,
  input  clk,
  output [31:0] ra,
  output [31:0] sp,
  output [31:0] t0,
  output [31:0] t1,
  output [31:0] t2,
  output [31:0] s0,
  output [31:0] s1,
  output [31:0] a0,
  output [31:0] Read_Data_1,
  output [31:0] Read_Data_2
);

  wire and_1_out, and_2_out, and_3_out, and_4_out, and_5_out, and_6_out, and_7_out, and_8_out, and_9_out,
       and_10_out, and_11_out, and_12_out, and_13_out, and_14_out, and_15_out, and_16_out, and_17_out,
       and_18_out, and_19_out, and_20_out, and_21_out, and_22_out, and_23_out, and_24_out, and_25_out,
       and_26_out, and_27_out, and_28_out, and_29_out, and_30_out, and_31_out, w0, w1, w2, w3, w4, w5, w6,
       w7, w8, w9, w10, w11, w12, w13, w14, w15, w16, w17, w18, w19, w20, w21, w22, w23, w24, w25, w26, w27,
       w28, w29, w30, w31;
  wire [31:0] multiplexer_1_out, multiplexer_2_out, multiplexer_3_out, multiplexer_4_out, multiplexer_5_out,
       multiplexer_6_out, multiplexer_7_out, multiplexer_8_out, multiplexer_9_out, multiplexer_10_out,
       multiplexer_11_out, multiplexer_12_out, multiplexer_13_out, multiplexer_14_out, multiplexer_15_out,
       multiplexer_16_out, multiplexer_17_out, multiplexer_18_out, multiplexer_19_out, multiplexer_20_out,
       multiplexer_21_out, multiplexer_22_out, multiplexer_23_out, multiplexer_24_out, multiplexer_25_out,
       multiplexer_27_out, multiplexer_28_out, multiplexer_29_out, multiplexer_30_out, multiplexer_32_out,
       multiplexer_33_out, reg_0, reg_3, reg_4, reg_11, reg_12, reg_13, reg_14, reg_15, reg_16, reg_17,
       reg_18, reg_19, reg_20, reg_21, reg_22, reg_23, reg_24, reg_25, reg_26, reg_27, reg_28, reg_29,
       reg_30, reg_31;

  and and_1 (and_1_out, w4, RegWEn);
  Multiplexer #(.width(32), .enable("false")) multiplexer_1 (
    .in0(s0), .in1(Write_Data), .out(multiplexer_1_out), .sel(and_2_out));
  and and_2 (and_2_out, w8, RegWEn);
  and and_3 (and_3_out, w12, RegWEn);
  and and_4 (and_4_out, w20, RegWEn);
  and and_5 (and_5_out, w28, RegWEn);
  Register #(.width(32)) register_1 (.D(reg_0), .clk(clk), .Q(reg_0));  // open: en, clr
  Multiplexer #(.width(32), .enable("false")) multiplexer_2 (
    .in0(reg_4), .in1(Write_Data), .out(multiplexer_2_out), .sel(and_1_out));
  Register #(.width(32)) register_2 (.D(multiplexer_2_out), .clk(clk), .Q(reg_4));  // open: en, clr
  Register #(.width(32)) register_3 (.D(multiplexer_1_out), .clk(clk), .Q(s0));  // open: en, clr
  Multiplexer #(.width(32), .enable("false")) multiplexer_3 (
    .in0(reg_12), .in1(Write_Data), .out(multiplexer_3_out), .sel(and_3_out));
  Register #(.width(32)) register_4 (.D(multiplexer_3_out), .clk(clk), .Q(reg_12));  // open: en, clr
  Multiplexer #(.width(32), .enable("false")) multiplexer_4 (
    .in0(reg_20), .in1(Write_Data), .out(multiplexer_4_out), .sel(and_4_out));
  Register #(.width(32)) register_5 (.D(multiplexer_4_out), .clk(clk), .Q(reg_20));  // open: en, clr
  Multiplexer #(.width(32), .enable("false")) multiplexer_5 (
    .in0(reg_28), .in1(Write_Data), .out(multiplexer_5_out), .sel(and_5_out));
  Register #(.width(32)) register_6 (.D(multiplexer_5_out), .clk(clk), .Q(reg_28));  // open: en, clr
  // Probe on and_6_out
  // Probe on multiplexer_6_out
  Multiplexer #(.width(32), .enable("false")) multiplexer_6 (
    .in0(ra), .in1(Write_Data), .out(multiplexer_6_out), .sel(and_6_out));
  and and_6 (and_6_out, w1, RegWEn);
  Register #(.width(32)) register_7 (.D(multiplexer_6_out), .clk(clk), .Q(ra));  // open: en, clr
  Multiplexer #(.width(32), .enable("false")) multiplexer_7 (
    .in0(t0), .in1(Write_Data), .out(multiplexer_7_out), .sel(and_7_out));
  and and_7 (and_7_out, w5, RegWEn);
  Register #(.width(32)) register_8 (.D(multiplexer_7_out), .clk(clk), .Q(t0));  // open: en, clr
  Multiplexer #(.width(32), .enable("false")) multiplexer_8 (
    .in0(s1), .in1(Write_Data), .out(multiplexer_8_out), .sel(and_8_out));
  and and_8 (and_8_out, w9, RegWEn);
  Multiplexer #(.width(32), .enable("false")) multiplexer_9 (
    .in0(reg_13), .in1(Write_Data), .out(multiplexer_9_out), .sel(and_9_out));
  and and_9 (and_9_out, w13, RegWEn);
  Multiplexer #(.width(32), .enable("false")) multiplexer_10 (
    .in0(reg_21), .in1(Write_Data), .out(multiplexer_10_out), .sel(and_10_out));
  and and_10 (and_10_out, w21, RegWEn);
  Multiplexer #(.width(32), .enable("false")) multiplexer_11 (
    .in0(reg_29), .in1(Write_Data), .out(multiplexer_11_out), .sel(and_11_out));
  and and_11 (and_11_out, w29, RegWEn);
  Register #(.width(32)) register_9 (.D(multiplexer_8_out), .clk(clk), .Q(s1));  // open: en, clr
  Register #(.width(32)) register_10 (.D(multiplexer_9_out), .clk(clk), .Q(reg_13));  // open: en, clr
  Register #(.width(32)) register_11 (.D(multiplexer_10_out), .clk(clk), .Q(reg_21));  // open: en, clr
  Register #(.width(32)) register_12 (.D(multiplexer_11_out), .clk(clk), .Q(reg_29));  // open: en, clr
  and and_12 (and_12_out, w2, RegWEn);
  Multiplexer #(.width(32), .enable("false")) multiplexer_12 (
    .in0(t1), .in1(Write_Data), .out(multiplexer_12_out), .sel(and_13_out));
  and and_13 (and_13_out, w6, RegWEn);
  Register #(.width(32)) register_13 (.D(multiplexer_12_out), .clk(clk), .Q(t1));  // open: en, clr
  and and_14 (and_14_out, w10, RegWEn);
  and and_15 (and_15_out, w14, RegWEn);
  and and_16 (and_16_out, w22, RegWEn);
  Multiplexer #(.width(32), .enable("false")) multiplexer_13 (
    .in0(sp), .in1(Write_Data), .out(multiplexer_13_out), .sel(and_12_out));
  Register #(.width(32)) register_14 (.D(multiplexer_13_out), .clk(clk), .Q(sp));  // open: en, clr
  Multiplexer #(.width(32), .enable("false")) multiplexer_14 (
    .in0(a0), .in1(Write_Data), .out(multiplexer_14_out), .sel(and_14_out));
  Register #(.width(32)) register_15 (.D(multiplexer_14_out), .clk(clk), .Q(a0));  // open: en, clr
  Multiplexer #(.width(32), .enable("false")) multiplexer_15 (
    .in0(reg_14), .in1(Write_Data), .out(multiplexer_15_out), .sel(and_15_out));
  Register #(.width(32)) register_16 (.D(multiplexer_15_out), .clk(clk), .Q(reg_14));  // open: en, clr
  Multiplexer #(.width(32), .enable("false")) multiplexer_16 (
    .in0(reg_22), .in1(Write_Data), .out(multiplexer_16_out), .sel(and_16_out));
  Register #(.width(32)) register_17 (.D(multiplexer_16_out), .clk(clk), .Q(reg_22));  // open: en, clr
  Multiplexer #(.width(32), .enable("false")) multiplexer_17 (
    .in0(reg_30), .in1(Write_Data), .out(multiplexer_17_out), .sel(and_17_out));
  and and_17 (and_17_out, w30, RegWEn);
  Register #(.width(32)) register_18 (.D(multiplexer_17_out), .clk(clk), .Q(reg_30));  // open: en, clr
  Multiplexer #(.width(32), .enable("false")) multiplexer_18 (
    .in0(t2), .in1(Write_Data), .out(multiplexer_18_out), .sel(and_18_out));
  and and_18 (and_18_out, w7, RegWEn);
  Multiplexer #(.width(32), .enable("false")) multiplexer_19 (
    .in0(reg_3), .in1(Write_Data), .out(multiplexer_19_out), .sel(and_19_out));
  and and_19 (and_19_out, w3, RegWEn);
  Register #(.width(32)) register_19 (.D(multiplexer_18_out), .clk(clk), .Q(t2));  // open: en, clr
  Multiplexer #(.width(32), .enable("false")) multiplexer_20 (
    .in0(reg_11), .in1(Write_Data), .out(multiplexer_20_out), .sel(and_20_out));
  and and_20 (and_20_out, w11, RegWEn);
  Multiplexer #(.width(32), .enable("false")) multiplexer_21 (
    .in0(reg_15), .in1(Write_Data), .out(multiplexer_21_out), .sel(and_21_out));
  and and_21 (and_21_out, w15, RegWEn);
  Multiplexer #(.width(32), .enable("false")) multiplexer_22 (
    .in0(reg_23), .in1(Write_Data), .out(multiplexer_22_out), .sel(and_22_out));
  and and_22 (and_22_out, w23, RegWEn);
  and and_23 (and_23_out, w31, RegWEn);
  Register #(.width(32)) register_20 (.D(multiplexer_19_out), .clk(clk), .Q(reg_3));  // open: en, clr
  Register #(.width(32)) register_21 (.D(multiplexer_20_out), .clk(clk), .Q(reg_11));  // open: en, clr
  Register #(.width(32)) register_22 (.D(multiplexer_21_out), .clk(clk), .Q(reg_15));  // open: en, clr
  Register #(.width(32)) register_23 (.D(multiplexer_22_out), .clk(clk), .Q(reg_23));  // open: en, clr
  Multiplexer #(.width(32), .enable("false")) multiplexer_23 (
    .in0(reg_31), .in1(Write_Data), .out(multiplexer_23_out), .sel(and_23_out));
  Register #(.width(32)) register_24 (.D(multiplexer_23_out), .clk(clk), .Q(reg_31));  // open: en, clr
  Multiplexer #(.width(32), .enable("false")) multiplexer_24 (
    .in0(reg_16), .in1(Write_Data), .out(multiplexer_24_out), .sel(and_24_out));
  and and_24 (and_24_out, w16, RegWEn);
  Multiplexer #(.width(32), .enable("false")) multiplexer_25 (
    .in0(reg_24), .in1(Write_Data), .out(multiplexer_25_out), .sel(and_25_out));
  and and_25 (and_25_out, w24, RegWEn);
  Register #(.width(32)) register_25 (.D(multiplexer_24_out), .clk(clk), .Q(reg_16));  // open: en, clr
  Register #(.width(32)) register_26 (.D(multiplexer_25_out), .clk(clk), .Q(reg_24));  // open: en, clr
  Multiplexer #(.select(5), .width(32), .enable("false")) multiplexer_26 (
    .in0(reg_0), .in1(ra), .in2(sp), .in3(reg_3), .in4(reg_4), .in5(t0), .in6(t1), .in7(t2), .in8(s0),
    .in9(s1), .in10(a0), .in11(reg_11), .in12(reg_12), .in13(reg_13), .in14(reg_14), .in15(reg_15),
    .in16(reg_16), .in17(reg_17), .in18(reg_18), .in19(reg_19), .in20(reg_20), .in21(reg_21), .in22(reg_22),
    .in23(reg_23), .in24(reg_24), .in25(reg_25), .in26(reg_26), .in27(reg_27), .in28(reg_28), .in29(reg_29),
    .in30(reg_30), .in31(reg_31), .out(Read_Data_1), .sel(rs1));
  and and_26 (and_26_out, w17, RegWEn);
  and and_27 (and_27_out, w25, RegWEn);
  Multiplexer #(.width(32), .enable("false")) multiplexer_27 (
    .in0(reg_17), .in1(Write_Data), .out(multiplexer_27_out), .sel(and_26_out));
  Register #(.width(32)) register_27 (.D(multiplexer_27_out), .clk(clk), .Q(reg_17));  // open: en, clr
  Multiplexer #(.width(32), .enable("false")) multiplexer_28 (
    .in0(reg_25), .in1(Write_Data), .out(multiplexer_28_out), .sel(and_27_out));
  Register #(.width(32)) register_28 (.D(multiplexer_28_out), .clk(clk), .Q(reg_25));  // open: en, clr
  Multiplexer #(.width(32), .enable("false")) multiplexer_29 (
    .in0(reg_18), .in1(Write_Data), .out(multiplexer_29_out), .sel(and_28_out));
  and and_28 (and_28_out, w18, RegWEn);
  Multiplexer #(.width(32), .enable("false")) multiplexer_30 (
    .in0(reg_26), .in1(Write_Data), .out(multiplexer_30_out), .sel(and_29_out));
  and and_29 (and_29_out, w26, RegWEn);
  Multiplexer #(.select(5), .width(32), .enable("false")) multiplexer_31 (
    .in0(reg_0), .in1(ra), .in2(sp), .in3(reg_3), .in4(reg_4), .in5(t0), .in6(t1), .in7(t2), .in8(s0),
    .in9(s1), .in10(a0), .in11(reg_11), .in12(reg_12), .in13(reg_13), .in14(reg_14), .in15(reg_15),
    .in16(reg_16), .in17(reg_17), .in18(reg_18), .in19(reg_19), .in20(reg_20), .in21(reg_21), .in22(reg_22),
    .in23(reg_23), .in24(reg_24), .in25(reg_25), .in26(reg_26), .in27(reg_27), .in28(reg_28), .in29(reg_29),
    .in30(reg_30), .in31(reg_31), .out(Read_Data_2), .sel(rs2));
  Register #(.width(32)) register_29 (.D(multiplexer_29_out), .clk(clk), .Q(reg_18));  // open: en, clr
  Register #(.width(32)) register_30 (.D(multiplexer_30_out), .clk(clk), .Q(reg_26));  // open: en, clr
  Demultiplexer #(.select(5), .enable("false")) demultiplexer_1 (
    .out0(w0), .out1(w1), .out2(w2), .out3(w3), .out4(w4), .out5(w5), .out6(w6), .out7(w7), .out8(w8),
    .out9(w9), .out10(w10), .out11(w11), .out12(w12), .out13(w13), .out14(w14), .out15(w15), .out16(w16),
    .out17(w17), .out18(w18), .out19(w19), .out20(w20), .out21(w21), .out22(w22), .out23(w23), .out24(w24),
    .out25(w25), .out26(w26), .out27(w27), .out28(w28), .out29(w29), .out30(w30), .out31(w31), .in(1'b1),
    .sel(rd));
  // Probe on w31
  and and_30 (and_30_out, w19, RegWEn);
  Multiplexer #(.width(32), .enable("false")) multiplexer_32 (
    .in0(reg_19), .in1(Write_Data), .out(multiplexer_32_out), .sel(and_30_out));
  Register #(.width(32)) register_31 (.D(multiplexer_32_out), .clk(clk), .Q(reg_19));  // open: en, clr
  Multiplexer #(.width(32), .enable("false")) multiplexer_33 (
    .in0(reg_27), .in1(Write_Data), .out(multiplexer_33_out), .sel(and_31_out));
  and and_31 (and_31_out, w27, RegWEn);
  Register #(.width(32)) register_32 (.D(multiplexer_33_out), .clk(clk), .Q(reg_27));  // open: en, clr
  // also tied to GND on the sheet: {reg_0[0], reg_0[1], reg_0[2], reg_0[3], reg_0[4], reg_0[5], reg_0[6], reg_0[7], reg_0[8], reg_0[9], reg_0[10], reg_0[11], reg_0[12], reg_0[13], reg_0[14], reg_0[15], reg_0[16], reg_0[17], reg_0[18], reg_0[19], reg_0[20], reg_0[21], reg_0[22], reg_0[23], reg_0[24], reg_0[25], reg_0[26], reg_0[27], reg_0[28], reg_0[29], reg_0[30], reg_0[31]}

  // Other names for the same wires on the sheet: read_data1[31:0] = Read_Data_1; read_data2[31:0] = Read_Data_2;
  //   read_reg1[4:0] = rs1; read_reg2[4:0] = rs2; write_en = RegWEn; write_reg[4:0] = rd

  // Notes on the sheet:
  //   INPUTS to your circuit
  //   DON'T CHANGE THE LOCATIONS OF THE INPUTS AND OUTPUTS!
  //   These are DEBUG/TEST outputs from your circuit.
  //   OUTPUTS from your circuit
endmodule
